# Fritzing sketch arduinoMicroSchema (saved by Fritzing 0.9.3b)

parts:
  JP3 = Header 8 [package=1x08_smd]
  JP5 = Header 6 [package=1x06_smd_straight_alt]
  JP6 = Header 1 [package=1x01_offset]
  JP7 = Header 1 [package=1x01_offset]
  JP8 = Header 1 [package=1x01_offset]
  JP9 = Header 1 [package=1x01_offset]
  Componente3 = Arduino Nano (Rev3.0)

nets:
  N1: JP3.1, Componente3.D9
  N2: JP3.2, Componente3.D8
  N3: JP3.3, Componente3.D7
  N4: JP3.4, Componente3.D6
  N5: JP3.5, Componente3.D5
  N6: JP3.6, Componente3.D4
  N7: JP3.7, Componente3.D3
  N8: JP3.8, Componente3.D2
  N9: JP5.1, Componente3.A2, Componente3.A1
  N10: JP5.2, Componente3.D13/SCK
  N11: JP5.3, Componente3.A0
  N12: JP5.4, Componente3.D12/MISO
  N13: JP5.5, Componente3.D11/MOSI
  N14: JP5.6, Componente3.D10
  N15: JP6.1, Componente3.GND
  N16: JP7.1, Componente3.D0/RX
  N17: JP8.1, Componente3.D1/TX
  N18: JP9.1, Componente3.VIN
